// Logisim project 4bit_full_adder_74283.circ as structural Verilog: 1 circuit, main circuit main
module main (
  input  in_1,
  input  in_2,
  input  in_3,
  input  in_4,
  input  in_5,
  input  in_6,
  input  in_7,
  input  in_8,
  input  in_9
);

  wire n74283_1_pin1, n74283_1_pin4, n74283_1_pin9, n74283_1_pin10, n74283_1_pin13;

  _74283 u_74283_1 (
    .pin1(n74283_1_pin1), .pin2(in_8), .pin3(in_3), .pin4(n74283_1_pin4), .pin5(in_4), .pin6(in_9),
    .pin15(in_7), .pin14(in_2), .pin13(n74283_1_pin13), .pin12(in_1), .pin11(in_6), .pin10(n74283_1_pin10),
    .pin9(n74283_1_pin9));  // open: pin7
  LED led_1 (.in(n74283_1_pin9));
  LED led_2 (.in(n74283_1_pin10));
  LED led_3 (.in(n74283_1_pin13));
  LED led_4 (.in(n74283_1_pin1));
  LED led_5 (.in(n74283_1_pin4));
endmodule
