// Logisim project BCD_exses_3.circ as structural Verilog: 1 circuit, main circuit main
module main (
  input  D,
  input  C,
  input  B,
  input  A
);

  wire and_1_out, and_2_out, and_3_out, and_4_out, not_1_out, not_2_out, not_3_out, or_1_out, or_2_out,
       or_3_out, or_4_out;

  not not_1 (not_1_out, B);
  not not_2 (not_2_out, D);
  and and_1 (and_1_out, D, C);
  or or_1 (or_1_out, D, C);
  and and_2 (and_2_out, not_1_out, or_1_out);
  not not_3 (not_3_out, or_1_out);
  and and_3 (and_3_out, B, not_3_out);
  and and_4 (and_4_out, B, or_1_out);
  or or_2 (or_2_out, and_1_out, not_3_out);
  or or_3 (or_3_out, and_2_out, and_3_out);
  or or_4 (or_4_out, and_4_out, A);
  LED led_1 (.in(not_2_out));
  LED led_2 (.in(or_2_out));
  LED led_3 (.in(or_3_out));

  // Notes on the sheet:
  //   Y
  //   Z
  //   X
  //   W
endmodule
