// Logisim project Bcd_4bit_fulladder.circ as structural Verilog: 1 circuit, main circuit main
module main (
  input  in_1,
  input  in_2,
  input  in_3,
  input  in_4,
  input  in_5,
  input  in_6,
  input  in_7,
  input  in_8,
  input  in_9,
  input  in_10
);

  wire and_1_out, and_2_out, n74283_1_pin1, n74283_1_pin4, n74283_1_pin9, n74283_1_pin10, n74283_1_pin13,
       n74283_2_pin1, n74283_2_pin4, n74283_2_pin10, n74283_2_pin13, or_1_out;

  LED led_1 (.in(or_1_out));
  or or_1 (or_1_out, n74283_1_pin9, and_1_out, and_2_out);
  _74283 u_74283_1 (
    .pin1(n74283_1_pin1), .pin2(in_8), .pin3(in_3), .pin4(n74283_1_pin4), .pin5(in_4), .pin6(in_9),
    .pin7(in_5), .pin15(in_7), .pin14(in_2), .pin13(n74283_1_pin13), .pin12(in_1), .pin11(in_6),
    .pin10(n74283_1_pin10), .pin9(n74283_1_pin9));
  _74283 u_74283_2 (
    .pin1(n74283_2_pin1), .pin2(or_1_out), .pin3(n74283_1_pin1), .pin4(n74283_2_pin4), .pin5(n74283_1_pin4),
    .pin6(in_10), .pin15(or_1_out), .pin14(n74283_1_pin13), .pin13(n74283_2_pin13), .pin12(n74283_1_pin10),
    .pin11(in_10), .pin10(n74283_2_pin10));  // open: pin7, pin9
  and and_1 (and_1_out, n74283_1_pin10, n74283_1_pin13);
  and and_2 (and_2_out, n74283_1_pin10, n74283_1_pin1);
  LED led_2 (.in(n74283_1_pin9));
  LED led_3 (.in(n74283_1_pin10));
  LED led_4 (.in(n74283_1_pin13));
  LED led_5 (.in(n74283_1_pin1));
  LED led_6 (.in(n74283_1_pin4));
  LED led_7 (.in(n74283_2_pin10));
  LED led_8 (.in(n74283_2_pin13));
  LED led_9 (.in(n74283_2_pin1));
  LED led_10 (.in(n74283_2_pin4));
endmodule
