// Logisim project Comparator_ic.circ as structural Verilog: 1 circuit, main circuit main
module main (
  input  [7:0] in_1,
  input  [7:0] in_2,
  output A_B,
  output out_4,
  output out_5
);

  Comparator comparator_1 (.a(in_1), .b(in_2), .gt(A_B), .eq(out_4), .lt(out_5));

  // Notes on the sheet:
  //   B>A
endmodule
