// Logisim project DMUX_ic.circ as structural Verilog: 1 circuit, main circuit main
module main (
  input  a,
  input  b,
  input  c,
  input  in_4,
  input  [1:0] in_5,
  output [3:0] D,
  output out_7,
  output out_8,
  output out_9,
  output out_10
);

  wire not_1_out, not_2_out;

  not not_1 (not_1_out, b);
  not not_2 (not_2_out, c);
  and and_1 (D[3], a, not_1_out, not_2_out);
  and and_2 (D[2], a, not_1_out, c);
  and and_3 (D[1], a, b, not_2_out);
  and and_4 (D[0], a, b, c);
  Demultiplexer #(.select(2)) demultiplexer_1 (
    .out0(out_7), .out1(out_8), .out2(out_9), .out3(out_10), .in(in_4), .sel(in_5));
endmodule
