// Logisim project Decoder_74138_ic.circ as structural Verilog: 1 circuit, main circuit main
module main (
  input  a,
  input  b,
  input  c,
  input  in_4,
  input  in_5,
  input  in_6,
  output [7:0] D,
  output out_8,
  output out_9,
  output out_10,
  output out_11,
  output out_12,
  output out_13,
  output out_14,
  output out_15
);

  wire not_1_out, not_2_out, not_3_out;

  not not_1 (not_1_out, a);
  not not_2 (not_2_out, b);
  not not_3 (not_3_out, c);
  and and_1 (D[7], not_1_out, not_2_out, not_3_out);
  and and_2 (D[6], not_1_out, not_2_out, c);
  and and_3 (D[5], not_1_out, b, not_3_out);
  and and_4 (D[4], not_1_out, b, c);
  and and_5 (D[3], a, not_2_out, not_3_out);
  and and_6 (D[2], a, not_2_out, c);
  and and_7 (D[1], a, b, not_3_out);
  and and_8 (D[0], a, b, c);
  _74138 u_74138_1 (
    .pin1(c), .pin2(b), .pin3(a), .pin4(in_4), .pin5(in_5), .pin6(in_6), .pin7(out_15), .pin15(out_12),
    .pin14(out_13), .pin13(out_11), .pin12(out_10), .pin11(out_8), .pin10(out_9), .pin9(out_14));

  // Notes on the sheet:
  //   Active low ic 
endmodule
