// Logisim project Encoder_OR_Gate_ic.circ as structural Verilog: 1 circuit, main circuit main
module main (
  input  in_1,
  input  in_2,
  input  in_3,
  input  in_4,
  input  in_5,
  input  in_6,
  input  in_7,
  input  in_8,
  output out_9,
  output out_10,
  output out_11
);

  wire n7432_1_pin3, n7432_1_pin6, n7432_1_pin11, n7432_2_pin2, n7432_2_pin6, n7432_2_pin8, or_1_out,
       or_2_out, or_3_out;

  _7432 u_7432_1 (
    .pin1(in_7), .pin2(in_8), .pin3(n7432_1_pin3), .pin4(in_3), .pin5(in_4), .pin6(n7432_1_pin6),
    .pin13(in_5), .pin12(in_6), .pin11(n7432_1_pin11), .pin10(n7432_1_pin11), .pin9(n7432_1_pin3),
    .pin8(out_9));
  or or_1 (or_1_out, in_5, in_6, in_7, in_8);
  or or_2 (or_2_out, in_3, in_4, in_7, in_8);
  or or_3 (or_3_out, in_2, in_4, in_6, in_8);
  LED led_1 (.in(or_1_out));
  LED led_2 (.in(or_3_out));
  LED led_3 (.in(or_2_out));
  _7432 u_7432_2 (
    .pin1(n7432_1_pin6), .pin2(n7432_2_pin2), .pin3(out_11), .pin4(in_2), .pin5(in_4), .pin6(n7432_2_pin6),
    .pin13(in_7), .pin12(in_8), .pin11(n7432_2_pin2), .pin10(in_6), .pin9(in_8), .pin8(n7432_2_pin8));
  _7432 u_7432_3 (
    .pin1(n7432_2_pin6), .pin2(n7432_2_pin8), .pin3(out_10));  // open: pin4, pin5, pin6, pin13, pin12, pin11, pin10, pin9, pin8
endmodule
