// Logisim project Full_Subtractor.circ as structural Verilog: 1 circuit, main circuit main
module main (
  input  in_1,
  input  in_2,
  input  in_3
);

  wire n7404_1_pin2, n7404_1_pin4, n7404_1_pin5, n7404_1_pin6, n7404_1_pin12, n7408_1_pin3, n7408_1_pin8,
       n7408_1_pin11, n7408_2_pin3, n7408_2_pin6, n7408_2_pin8, n7408_2_pin11, n7432_1_pin6, n7432_1_pin8,
       n7432_1_pin11;

  _7404 u_7404_1 (
    .pin1(in_2), .pin2(n7404_1_pin2), .pin3(in_3), .pin4(n7404_1_pin4), .pin5(n7404_1_pin5),
    .pin6(n7404_1_pin6), .pin13(in_1), .pin12(n7404_1_pin12));  // open: pin11, pin10, pin9, pin8
  _7408 u_7408_1 (
    .pin1(in_3), .pin2(in_2), .pin3(n7408_1_pin3), .pin13(n7404_1_pin12), .pin12(in_2),
    .pin11(n7408_1_pin11), .pin10(n7404_1_pin12), .pin9(in_3), .pin8(n7408_1_pin8));  // open: pin4, pin5, pin6
  _7408 u_7408_2 (
    .pin1(n7404_1_pin2), .pin2(in_1), .pin3(n7408_2_pin3), .pin4(n7404_1_pin4), .pin5(n7404_1_pin5),
    .pin6(n7408_2_pin6), .pin13(n7404_1_pin12), .pin12(in_2), .pin11(n7408_2_pin11), .pin10(n7404_1_pin6),
    .pin9(in_3), .pin8(n7408_2_pin8));
  _7432 u_7432_1 (
    .pin1(n7408_2_pin3), .pin2(n7408_2_pin11), .pin3(n7404_1_pin5), .pin4(n7408_2_pin6), .pin5(n7408_2_pin8),
    .pin6(n7432_1_pin6), .pin13(n7408_1_pin11), .pin12(n7408_1_pin8), .pin11(n7432_1_pin11),
    .pin10(n7432_1_pin11), .pin9(n7408_1_pin3), .pin8(n7432_1_pin8));
  LED led_1 (.in(n7432_1_pin8));
  LED led_2 (.in(n7432_1_pin6));
endmodule
