// Logisim project Half_Full_Subtractor_ic.circ as structural Verilog: 1 circuit, main circuit main
module main (
  input  in_1,
  input  in_2,
  input  in_3,
  input  in_4,
  input  in_5,
  output out_6,
  output out_7,
  output out_8,
  output out_9
);

  wire and_1_out, and_2_out, and_3_out, and_4_out, n7408_1_pin3, n7408_1_pin6, n7408_2_pin3, n7408_2_pin6,
       n7408_2_pin11, n7432_1_pin3, n7432_2_pin3, n7432_2_pin6, n7486_1_pin3, n7486_1_pin6, not_1_out,
       not_2_out, not_3_out, not_4_out, xor_1_out;

  not not_1 (not_1_out, in_2);
  not not_2 (not_2_out, in_1);
  not not_3 (not_3_out, in_3);
  _7486 u_7486_1 (
    .pin1(in_4), .pin2(in_3), .pin3(n7486_1_pin3), .pin4(n7486_1_pin3), .pin5(in_5), .pin6(n7486_1_pin6));  // open: pin13, pin12, pin11, pin10, pin9, pin8
  and and_1 (and_1_out, not_3_out, in_4);
  and and_2 (and_2_out, not_3_out, in_5);
  and and_3 (and_3_out, in_4, in_5);
  _7408 u_7408_1 (
    .pin1(in_1), .pin2(not_1_out), .pin3(n7408_1_pin3), .pin4(not_2_out), .pin5(in_2), .pin6(n7408_1_pin6));  // open: pin13, pin12, pin11, pin10, pin9, pin8
  xor xor_1 (xor_1_out, in_3, in_4);
  and and_4 (and_4_out, in_1, not_1_out);
  and and_5 (out_7, in_2, not_2_out);
  not not_4 (not_4_out, in_3);
  xor xor_2 (out_8, xor_1_out, in_5);
  _7432 u_7432_1 (
    .pin1(n7408_1_pin3), .pin2(n7408_1_pin6), .pin3(n7432_1_pin3));  // open: pin4, pin5, pin6, pin13, pin12, pin11, pin10, pin9, pin8
  _7408 u_7408_2 (
    .pin1(not_4_out), .pin2(in_4), .pin3(n7408_2_pin3), .pin4(not_4_out), .pin5(in_5), .pin6(n7408_2_pin6),
    .pin13(in_4), .pin12(in_5), .pin11(n7408_2_pin11));  // open: pin10, pin9, pin8
  or or_1 (out_6, and_4_out, out_7);
  or or_2 (out_9, and_1_out, and_2_out, and_3_out);
  LED led_1 (.in(n7486_1_pin6));
  LED led_2 (.in(n7432_1_pin3));
  LED led_3 (.in(n7408_1_pin6));
  _7432 u_7432_2 (
    .pin1(n7408_2_pin3), .pin2(n7408_2_pin6), .pin3(n7432_2_pin3), .pin4(n7432_2_pin3), .pin5(n7408_2_pin11),
    .pin6(n7432_2_pin6));  // open: pin13, pin12, pin11, pin10, pin9, pin8
  LED led_4 (.in(n7432_2_pin6));
endmodule
