// Logisim project Half_Full_adder_using_ic.circ as structural Verilog: 1 circuit, main circuit main
module main (
  input  in_1,
  input  in_2,
  input  in_3,
  input  in_4,
  input  in_5,
  output out_6,
  output out_7,
  output out_8,
  output out_9
);

  wire and_1_out, and_2_out, and_3_out, n7408_1_pin3, n7408_1_pin6, n7486_1_pin3, or_1_out, xor_1_out,
       xor_2_out, xor_3_out;

  _7486 u_7486_1 (
    .pin1(in_3), .pin2(in_4), .pin3(n7486_1_pin3), .pin4(n7486_1_pin3), .pin5(in_5), .pin6(out_8));  // open: pin13, pin12, pin11, pin10, pin9, pin8
  and and_1 (and_1_out, in_1, in_2);
  _7486 u_7486_2 (
    .pin1(in_1), .pin2(in_2), .pin3(out_6));  // open: pin4, pin5, pin6, pin13, pin12, pin11, pin10, pin9, pin8
  xor xor_1 (xor_1_out, in_1, in_2);
  xor xor_2 (xor_2_out, in_3, in_4);
  and and_2 (and_2_out, in_3, in_4);
  LED led_1 (.in(xor_1_out));
  LED led_2 (.in(and_1_out));
  xor xor_3 (xor_3_out, xor_2_out, in_5);
  and and_3 (and_3_out, xor_2_out, in_5);
  _7408 u_7408_1 (
    .pin1(in_3), .pin2(in_4), .pin3(n7408_1_pin3), .pin4(n7486_1_pin3), .pin5(in_5), .pin6(n7408_1_pin6));  // open: pin13, pin12, pin11, pin10, pin9, pin8
  _7408 u_7408_2 (
    .pin1(in_1), .pin2(in_2), .pin3(out_7));  // open: pin4, pin5, pin6, pin13, pin12, pin11, pin10, pin9, pin8
  LED led_3 (.in(xor_3_out));
  or or_1 (or_1_out, and_3_out, and_2_out);
  _7432 u_7432_1 (
    .pin1(n7408_1_pin6), .pin2(n7408_1_pin3), .pin3(out_9));  // open: pin4, pin5, pin6, pin13, pin12, pin11, pin10, pin9, pin8
  LED led_4 (.in(or_1_out));

  // Notes on the sheet:
  //   Half Adder
  //   Full Adder
endmodule
