// Logisim project Jk_master_slave.circ as structural Verilog: 1 circuit, main circuit main
module main (
  input  in_1,
  input  in_2
);

  wire clock_1_out, j_k_ff_1_q, j_k_ff_1_qn, j_k_ff_2_q, j_k_ff_2_qn, nand_1_out, nand_2_out, nand_3_out,
       nand_4_out, nand_5_out, nand_6_out, nand_7_out, nand_8_out, nand_9_out;

  Clock clock_1 (.out(clock_1_out));
  nand nand_1 (nand_1_out, in_1, nand_9_out, clock_1_out);
  nand nand_2 (nand_2_out, clock_1_out, nand_8_out, in_2);
  nand nand_3 (nand_3_out, clock_1_out, clock_1_out);
  J_K_Flip_Flop j_k_ff_1 (
    .J(in_1), .K(in_2), .clk(clock_1_out), .Q(j_k_ff_1_q), .Qn(j_k_ff_1_qn));  // open: preset, reset
  nand nand_4 (nand_4_out, nand_1_out, nand_5_out);
  nand nand_5 (nand_5_out, nand_4_out, nand_2_out);
  J_K_Flip_Flop j_k_ff_2 (
    .J(j_k_ff_1_q), .K(j_k_ff_1_qn), .clk(nand_3_out), .Q(j_k_ff_2_q), .Qn(j_k_ff_2_qn));  // open: preset, reset
  LED led_1 (.in(j_k_ff_2_q));
  LED led_2 (.in(j_k_ff_2_qn));
  nand nand_6 (nand_6_out, nand_4_out, nand_3_out);
  nand nand_7 (nand_7_out, nand_3_out, nand_5_out);
  nand nand_8 (nand_8_out, nand_6_out, nand_9_out);
  nand nand_9 (nand_9_out, nand_8_out, nand_7_out);
  LED led_3 (.in(nand_8_out));
  LED led_4 (.in(nand_9_out));
endmodule
