// Logisim project Mux_DMux_ic.circ as structural Verilog: 1 circuit, main circuit main
module main (
  input  in_1,
  input  in_2,
  input  in_3,
  input  in_4,
  input  [1:0] in_5,
  output out_6,
  output out_7,
  output out_8,
  output out_9
);

  wire multiplexer_1_out;

  Multiplexer #(.select(2)) multiplexer_1 (
    .in0(in_1), .in1(in_2), .in2(in_3), .in3(in_4), .out(multiplexer_1_out), .sel(in_5));
  Demultiplexer #(.select(2)) demultiplexer_1 (
    .out0(out_6), .out1(out_7), .out2(out_8), .out3(out_9), .in(multiplexer_1_out), .sel(in_5));
endmodule
