// Logisim project Riple_binary_counter.circ as structural Verilog: 1 circuit, main circuit main
module main (
  input  in_1,
  input  in_2,
  output out_3,
  output out_4,
  output out_5,
  output out_6,
  output out_7,
  output out_8,
  output out_9,
  output out_10
);

  wire and_1_out, and_2_out, and_3_out, clock_1_out, not_1_out, not_2_out, not_3_out, not_4_out;

  Clock clock_1 (.out(clock_1_out));
  J_K_Flip_Flop j_k_ff_1 (.J(in_1), .K(in_1), .clk(not_1_out), .Q(out_6));  // open: Qn, preset, reset
  not not_1 (not_1_out, clock_1_out);
  not not_2 (not_2_out, out_6);
  J_K_Flip_Flop j_k_ff_2 (.J(in_1), .K(in_1), .clk(not_2_out), .Q(out_3));  // open: Qn, preset, reset
  T_Flip_Flop t_ff_1 (.T(in_2), .clk(clock_1_out), .Q(out_10));  // open: Qn, reset, preset
  not not_3 (not_3_out, out_3);
  and and_1 (and_1_out, in_2, out_10);
  J_K_Flip_Flop j_k_ff_3 (.J(in_1), .K(in_1), .clk(not_3_out), .Q(out_4));  // open: Qn, preset, reset
  T_Flip_Flop t_ff_2 (.T(and_1_out), .clk(clock_1_out), .Q(out_8));  // open: Qn, reset, preset
  and and_2 (and_2_out, out_8, and_1_out);
  not not_4 (not_4_out, out_4);
  T_Flip_Flop t_ff_3 (.T(and_2_out), .clk(clock_1_out), .Q(out_9));  // open: Qn, reset, preset
  J_K_Flip_Flop j_k_ff_4 (.J(in_1), .K(in_1), .clk(not_4_out), .Q(out_5));  // open: Qn, preset, reset
  T_Flip_Flop t_ff_4 (.T(and_3_out), .clk(clock_1_out), .Q(out_7));  // open: Qn, reset, preset
  and and_3 (and_3_out, out_9, and_2_out);

  // Notes on the sheet:
  //   Asyconous Counter
  //   Synconous Counter
endmodule
