// Logisim project SR_Flip_Flop_ic.circ as structural Verilog: 1 circuit, main circuit main
module main (
  input  in_1,
  input  in_2,
  input  in_3,
  input  in_4,
  output out_5,
  output out_6,
  output out_7,
  output out_8,
  output out_9,
  output out_10
);

  wire and_1_out, and_2_out, clock_1_out, clock_2_out, n7400_1_pin3, n7400_1_pin11, nand_1_out, nand_2_out;

  Clock clock_1 (.out(clock_1_out));
  Clock clock_2 (.out(clock_2_out));
  and and_1 (and_1_out, in_1, clock_1_out);
  and and_2 (and_2_out, clock_1_out, in_2);
  nand nand_1 (nand_1_out, in_3, clock_2_out);
  nand nand_2 (nand_2_out, clock_2_out, in_4);
  _7400 u_7400_1 (
    .pin1(in_4), .pin2(clock_2_out), .pin3(n7400_1_pin3), .pin4(n7400_1_pin3), .pin5(out_9), .pin6(out_10),
    .pin13(clock_2_out), .pin12(in_3), .pin11(n7400_1_pin11), .pin10(n7400_1_pin11), .pin9(out_10),
    .pin8(out_9));
  nor nor_1 (out_5, and_1_out, out_6);
  nor nor_2 (out_6, out_5, and_2_out);
  nand nand_3 (out_7, nand_1_out, out_8);
  nand nand_4 (out_8, out_7, nand_2_out);
endmodule
