// Logisim project magnitude_comparator_4bit.circ as structural Verilog: 1 circuit, main circuit main
module main (
  input  in_1,
  input  in_2,
  input  in_3,
  input  in_4,
  input  in_5,
  input  in_6,
  input  in_7,
  input  in_8
);

  wire and_1_out, and_2_out, and_3_out, and_4_out, and_5_out, and_6_out, and_7_out, and_8_out, and_9_out,
       and_10_out, and_11_out, and_12_out, and_13_out, and_14_out, and_15_out, nor_1_out, nor_2_out,
       nor_3_out, nor_4_out, not_1_out, not_2_out, not_3_out, not_4_out, not_5_out, not_6_out, not_7_out,
       not_8_out, or_1_out, or_2_out;

  not not_1 (not_1_out, in_1);
  not not_2 (not_2_out, in_2);
  not not_3 (not_3_out, in_3);
  not not_4 (not_4_out, in_4);
  not not_5 (not_5_out, in_5);
  not not_6 (not_6_out, in_6);
  not not_7 (not_7_out, in_7);
  not not_8 (not_8_out, in_8);
  and and_1 (and_1_out, not_1_out, in_2);
  and and_2 (and_2_out, not_2_out, in_1);
  and and_3 (and_3_out, not_3_out, in_4);
  and and_4 (and_4_out, not_4_out, in_3);
  and and_5 (and_5_out, not_5_out, in_6);
  and and_6 (and_6_out, not_6_out, in_5);
  and and_7 (and_7_out, not_7_out, in_8);
  and and_8 (and_8_out, not_8_out, in_7);
  nor nor_1 (nor_1_out, and_3_out, and_4_out);
  nor nor_2 (nor_2_out, and_5_out, and_6_out);
  nor nor_3 (nor_3_out, and_7_out, and_8_out);
  nor nor_4 (nor_4_out, and_1_out, and_2_out);
  and and_9 (and_9_out, nor_4_out, and_3_out);
  and and_10 (and_10_out, nor_4_out, and_4_out);
  and and_11 (and_11_out, and_5_out, nor_4_out, nor_1_out);
  and and_12 (and_12_out, nor_4_out, and_6_out, nor_1_out);
  and and_13 (and_13_out, and_7_out, nor_4_out, nor_1_out, nor_2_out);
  and and_14 (and_14_out, and_8_out, nor_4_out, nor_1_out, nor_2_out);
  or or_1 (or_1_out, and_1_out, and_9_out, and_11_out, and_13_out);
  or or_2 (or_2_out, and_2_out, and_10_out, and_12_out, and_14_out);
  and and_15 (and_15_out, nor_4_out, nor_1_out, nor_2_out, nor_3_out);
  LED led_1 (.in(or_1_out));
  LED led_2 (.in(or_2_out));
  LED led_3 (.in(and_15_out));

  // Notes on the sheet:
  //   A<B
  //   A>B
endmodule
