// Logisim project parity_check.circ as structural Verilog: 1 circuit, main circuit main
module main (
  input  in_1,
  input  in_2,
  input  in_3,
  input  in_4
);

  wire n7404_1_pin1, n7404_1_pin2, n7404_1_pin10, n7404_1_pin11, n7404_1_pin12, n7404_1_pin13;

  _7404 u_7404_1 (
    .pin1(n7404_1_pin1), .pin2(n7404_1_pin2), .pin13(n7404_1_pin13), .pin12(n7404_1_pin12),
    .pin11(n7404_1_pin11), .pin10(n7404_1_pin10));  // open: pin3, pin4, pin5, pin6, pin9, pin8
  _7486 u_7486_1 (
    .pin1(n7404_1_pin10), .pin2(in_4), .pin3(n7404_1_pin1), .pin13(in_1), .pin12(in_2),
    .pin11(n7404_1_pin13), .pin10(n7404_1_pin12), .pin9(in_3), .pin8(n7404_1_pin11));  // open: pin4, pin5, pin6
  LED led_1 (.in(n7404_1_pin2));
endmodule
