// Logisim project parity_generate.circ as structural Verilog: 1 circuit, main circuit main
module main (
  input  in_1,
  input  in_2,
  input  in_3
);

  wire n7404_1_pin12, n7404_1_pin13, n7486_1_pin11;

  _7404 u_7404_1 (
    .pin13(n7404_1_pin13), .pin12(n7404_1_pin12));  // open: pin1, pin2, pin3, pin4, pin5, pin6, pin11, pin10, pin9, pin8
  _7486 u_7486_1 (
    .pin13(in_1), .pin12(in_2), .pin11(n7486_1_pin11), .pin10(n7486_1_pin11), .pin9(in_3),
    .pin8(n7404_1_pin13));  // open: pin1, pin2, pin3, pin4, pin5, pin6
  LED led_1 (.in(n7404_1_pin12));
endmodule
