// Logisim project universal_shift_register.circ as structural Verilog: 1 circuit, main circuit main
module main (
  input  in_1,
  input  in_2,
  input  in_3,
  input  in_4,
  input  in_5,
  input  in_6,
  input  in_7,
  input  in_8,
  input  in_9,
  input  in_10,
  input  in_11,
  input  left_shift_input,
  input  [1:0] in_13,
  input  [1:0] in_14,
  input  in_15,
  input  reset,
  output out_17,
  output out_18,
  output out_19,
  output out_20,
  output out_21,
  output out_22,
  output out_23,
  output out_24
);

  wire clock_1_out, clock_2_out, multiplexer_1_out, multiplexer_2_out, multiplexer_3_out, multiplexer_4_out,
       multiplexer_5_out, multiplexer_6_out, multiplexer_7_out, multiplexer_8_out;

  Clock clock_1 (.out(clock_1_out));
  Multiplexer #(.select(2)) multiplexer_1 (
    .in0(out_19), .in1(in_3), .in2(out_20), .in3(in_5), .out(multiplexer_1_out), .sel(in_13));
  Multiplexer #(.select(2)) multiplexer_2 (
    .in0(out_20), .in1(out_19), .in2(out_22), .in3(in_6), .out(multiplexer_2_out), .sel(in_13));
  Multiplexer #(.select(2)) multiplexer_3 (
    .in0(out_22), .in1(out_20), .in2(out_24), .in3(in_7), .out(multiplexer_3_out), .sel(in_13));
  Multiplexer #(.select(2)) multiplexer_4 (
    .in0(out_24), .in1(out_22), .in2(left_shift_input), .in3(in_8), .out(multiplexer_4_out), .sel(in_13));
  D_Flip_Flop d_ff_1 (.D(multiplexer_1_out), .clk(clock_1_out), .Q(out_19), .reset(reset));  // open: Qn, preset
  D_Flip_Flop d_ff_2 (.D(multiplexer_2_out), .clk(clock_1_out), .Q(out_20), .reset(reset));  // open: Qn, preset
  D_Flip_Flop d_ff_3 (.D(multiplexer_3_out), .clk(clock_1_out), .Q(out_22), .reset(reset));  // open: Qn, preset
  D_Flip_Flop d_ff_4 (.D(multiplexer_4_out), .clk(clock_1_out), .Q(out_24), .reset(reset));  // open: Qn, preset
  Multiplexer #(.select(2)) multiplexer_5 (
    .in0(out_17), .in1(in_1), .in2(out_18), .in3(in_2), .out(multiplexer_5_out), .sel(in_14));
  Multiplexer #(.select(2)) multiplexer_6 (
    .in0(out_18), .in1(out_17), .in2(out_21), .in3(in_4), .out(multiplexer_6_out), .sel(in_14));
  Multiplexer #(.select(2)) multiplexer_7 (
    .in0(out_21), .in1(out_18), .in2(out_23), .in3(in_9), .out(multiplexer_7_out), .sel(in_14));
  Multiplexer #(.select(2)) multiplexer_8 (
    .in0(out_23), .in1(out_21), .in2(in_10), .in3(in_11), .out(multiplexer_8_out), .sel(in_14));
  Clock clock_2 (.out(clock_2_out));
  D_Flip_Flop d_ff_5 (.D(multiplexer_5_out), .clk(clock_2_out), .Q(out_17), .reset(in_15));  // open: Qn, preset
  D_Flip_Flop d_ff_6 (.D(multiplexer_6_out), .clk(clock_2_out), .Q(out_18), .reset(in_15));  // open: Qn, preset
  D_Flip_Flop d_ff_7 (.D(multiplexer_7_out), .clk(clock_2_out), .Q(out_21), .reset(in_15));  // open: Qn, preset
  D_Flip_Flop d_ff_8 (.D(multiplexer_8_out), .clk(clock_2_out), .Q(out_23), .reset(in_15));  // open: Qn, preset

  // Notes on the sheet:
  //   selection
  //   right-shift input
  //   clock
  //   Universal shift register
  //   0 1 right-shift
  //   1 0 left-shift
  //   0 0 parallel output
  //   1 1 parallel load
endmodule
